// Logisim project practicWork2MUX_2_to_1.circ as structural Verilog: 1 circuit, main circuit main
module main (
  input  I0,
  input  S,
  input  I1,
  output out_4
);

  wire and_1_out, and_2_out, not_1_out;

  and and_1 (and_1_out, I0, not_1_out);
  not not_1 (not_1_out, S);
  and and_2 (and_2_out, S, I1);
  or or_1 (out_4, and_1_out, and_2_out);
endmodule
