// Logisim project practicWork2fullAdder.circ as structural Verilog: 1 circuit, main circuit main
module main (
  input  A,
  input  B,
  input  Cin,
  output Cout,
  output Sum
);

  wire and_1_out, and_2_out, xor_2_out;

  and and_1 (and_1_out, A, B);
  xor xor_1 (Sum, xor_2_out, Cin);
  and and_2 (and_2_out, Cin, xor_2_out);
  xor xor_2 (xor_2_out, A, B);
  or or_1 (Cout, and_1_out, and_2_out);
endmodule
